// Logisim project 3진법 계산기.circ as structural Verilog: 2 circuits, main circuit main
module main (
  input  a1,
  input  a0,
  input  b1,
  input  b0,
  input  C1,
  input  C0,
  output [1:0] Sum,
  output Carry
);

  wire ha_1_carry, ha_1_s0, ha_1_s1, ha_2_carry;

  HA ha_1 (.a1(a1), .a0(a0), .b1(b1), .b0(b0), .Carry(ha_1_carry), .S0(ha_1_s0), .S1(ha_1_s1));
  HA ha_2 (.a1(ha_1_s1), .a0(ha_1_s0), .b1(C1), .b0(C0), .Carry(ha_2_carry), .S0(Sum[0]), .S1(Sum[1]));
  or or_1 (Carry, ha_2_carry, ha_1_carry);
endmodule

module HA (
  input  a1,
  input  a0,
  input  b1,
  input  b0,
  output S0,
  output S1,
  output Carry
);

  wire _00_2_out, _00_out, _01_2_out, _01_3_out, _01_4_out, _01_5_out, _01_out, _10_2_out, _10_3_out,
       _10_4_out, _10_5_out, _10_out, and_1_out, and_2_out, and_3_out, not_1_out, not_2_out, not_3_out,
       not_4_out, not_5_out, not_6_out, not_7_out, not_8_out;

  not not_1 (not_1_out, a1);
  and _00 (_00_out, not_1_out, not_2_out);
  not not_2 (not_2_out, a0);
  not not_3 (not_3_out, a1);
  and _01 (_01_out, not_3_out, a0);
  and _10 (_10_out, a1, not_4_out);
  not not_4 (not_4_out, a0);
  not not_5 (not_5_out, b1);
  and _00_2 (_00_2_out, not_5_out, not_6_out);
  not not_6 (not_6_out, b0);
  not not_7 (not_7_out, b1);
  and _01_2 (_01_2_out, not_7_out, b0);
  and _10_2 (_10_2_out, b1, not_8_out);
  not not_8 (not_8_out, b0);
  and _01_3 (_01_3_out, _00_out, _01_2_out);
  and _01_4 (_01_4_out, _01_out, _00_2_out);
  and _01_5 (_01_5_out, _10_out, _10_2_out);
  and _10_3 (_10_3_out, _00_out, _10_2_out);
  and _10_4 (_10_4_out, _01_out, _01_2_out);
  and _10_5 (_10_5_out, _10_out, _00_2_out);
  and and_1 (and_1_out, _01_out, _10_2_out);
  and and_2 (and_2_out, _10_out, _01_2_out);
  and and_3 (and_3_out, _10_out, _10_2_out);
  or or_1 (S0, _01_3_out, _01_4_out, _01_5_out);
  or or_2 (S1, _10_3_out, _10_4_out, _10_5_out);
  or or_3 (Carry, and_1_out, and_2_out, and_3_out);
endmodule
