// Logisim project 4bit ALU.circ as structural Verilog
module _4x1_MUX (
  input  S1,
  input  S0,
  input  I0,
  input  I1,
  input  I2,
  input  I3,
  output O
);

  wire _00_out, _01_out, _10_out, _11_out, not_1_out, not_2_out;

  not not_1 (not_1_out, S1);
  not not_2 (not_2_out, S0);
  and _00 (_00_out, I0, not_1_out, not_2_out);
  and _01 (_01_out, I1, not_1_out, S0);
  and _10 (_10_out, I2, S1, not_2_out);
  and _11 (_11_out, I3, S1, S0);
  or or_1 (O, _00_out, _01_out, _10_out, _11_out);
endmodule

module _1bit_LU (
  input  I0,
  input  I1,
  input  S1,
  input  S0,
  output out_5
);

  wire and_1_out, not_1_out, or_1_out, xor_1_out;

  and and_1 (and_1_out, I0, I1);
  or or_1 (or_1_out, I0, I1);
  xor xor_1 (xor_1_out, I0, I1);
  not not_1 (not_1_out, I0);
  _4x1_MUX u_4x1_mux_1 (.S1(S1), .S0(S0), .I0(and_1_out), .I1(or_1_out), .I2(xor_1_out), .I3(not_1_out), .O(out_5));
endmodule

// 4 LU
module _4bit_LU (
  input  [3:0] in_1,
  input  [3:0] in_2,
  input  S1,
  input  S0,
  output [3:0] out_5
);

  _1bit_LU u_1bit_lu_1 (.I0(in_1[0]), .I1(in_2[0]), .S1(S1), .S0(S0), .out_5(out_5[0]));
  _1bit_LU u_1bit_lu_2 (.I0(in_1[1]), .I1(in_2[1]), .S1(S1), .S0(S0), .out_5(out_5[1]));
  _1bit_LU u_1bit_lu_3 (.I0(in_1[2]), .I1(in_2[2]), .S1(S1), .S0(S0), .out_5(out_5[2]));
  _1bit_LU u_1bit_lu_4 (.I0(in_1[3]), .I1(in_2[3]), .S1(S1), .S0(S0), .out_5(out_5[3]));
endmodule

// 4 SH
module _4bit_shifter (
  input  SLin,
  input  [3:0] in_2,
  input  SRin,
  input  S1,
  input  S0,
  output [3:0] out_6
);

  _4x1_MUX u_4x1_mux_1 (.S1(S1), .S0(S0), .I0(in_2[0]), .I1(SLin), .I2(in_2[1]), .O(out_6[0]));  // open: I3
  _4x1_MUX u_4x1_mux_2 (.S1(S1), .S0(S0), .I0(in_2[1]), .I1(in_2[0]), .I2(in_2[2]), .O(out_6[1]));  // open: I3
  _4x1_MUX u_4x1_mux_3 (.S1(S1), .S0(S0), .I0(in_2[2]), .I1(in_2[1]), .I2(in_2[3]), .O(out_6[2]));  // open: I3
  _4x1_MUX u_4x1_mux_4 (.S1(S1), .S0(S0), .I0(in_2[3]), .I1(in_2[2]), .I2(SRin), .O(out_6[3]));  // open: I3

  // Notes on the sheet:
  //   shifter 규칙
  //   s1 s0
  //   0 0 = pass
  //   0 1 = shift left
  //   1 0 = shift right
endmodule

module SR_latch (
  input  R,
  input  E,
  input  S,
  output Q,
  output nQ
);

  wire and_1_out, and_2_out;

  and and_1 (and_1_out, R, E);
  and and_2 (and_2_out, E, S);
  nor nor_1 (Q, and_1_out, nQ);
  nor nor_2 (nQ, Q, and_2_out);
endmodule

module D_latch (
  input  D,
  input  E,
  output Q,
  output nQ
);

  wire and_1_out, and_2_out, not_1_out;

  not not_1 (not_1_out, D);
  and and_1 (and_1_out, not_1_out, E);
  and and_2 (and_2_out, E, D);
  nor nor_1 (nQ, Q, and_2_out);
  nor nor_2 (Q, and_1_out, nQ);
endmodule

// FA
module full_adder (
  input  A,
  input  B,
  input  Ci,
  output S,
  output Co
);

  wire and_1_out, and_2_out, and_3_out, and_4_out, and_5_out, and_6_out, and_7_out, not_1_out, not_2_out,
       not_3_out, not_4_out, not_5_out, not_6_out;

  not not_1 (not_1_out, A);
  not not_2 (not_2_out, B);
  not not_3 (not_3_out, A);
  not not_4 (not_4_out, Ci);
  not not_5 (not_5_out, B);
  not not_6 (not_6_out, Ci);
  and and_1 (and_1_out, B, Ci);
  and and_2 (and_2_out, A, Ci);
  and and_3 (and_3_out, A, B);
  and and_4 (and_4_out, not_1_out, not_2_out, Ci);
  and and_5 (and_5_out, not_3_out, B, not_4_out);
  and and_6 (and_6_out, A, not_5_out, not_6_out);
  and and_7 (and_7_out, A, B, Ci);
  or or_1 (Co, and_1_out, and_2_out, and_3_out);
  or or_2 (S, and_4_out, and_5_out, and_6_out, and_7_out);
endmodule

// 1 AU
module _1bit_AU (
  input  Ci,
  input  A,
  input  B,
  input  S1,
  input  S0,
  output F,
  output Co
);

  wire n4x1_mux_1_o, not_1_out;

  _4x1_MUX u_4x1_mux_1 (.S1(S1), .S0(S0), .I0(1'b0), .I1(B), .I2(not_1_out), .I3(1'b1), .O(n4x1_mux_1_o));
  not not_1 (not_1_out, B);
  full_adder full_adder_1 (.A(A), .B(n4x1_mux_1_o), .Ci(Ci), .S(F), .Co(Co));
endmodule

// 4 AU
module _4bit_AU (
  input  Cin,
  input  [3:0] A,
  input  [3:0] B,
  input  in_4,
  input  in_5,
  output [3:0] out_6,
  output V,
  output Co
);

  wire n1bit_au_1_co, n1bit_au_2_co, n1bit_au_3_co;

  _1bit_AU u_1bit_au_1 (.Ci(Cin), .A(A[0]), .B(B[0]), .S1(in_4), .S0(in_5), .F(out_6[0]), .Co(n1bit_au_1_co));
  _1bit_AU u_1bit_au_2 (.Ci(n1bit_au_1_co), .A(A[1]), .B(B[1]), .S1(in_4), .S0(in_5), .F(out_6[1]), .Co(n1bit_au_2_co));
  _1bit_AU u_1bit_au_3 (.Ci(n1bit_au_2_co), .A(A[2]), .B(B[2]), .S1(in_4), .S0(in_5), .F(out_6[2]), .Co(n1bit_au_3_co));
  _1bit_AU u_1bit_au_4 (.Ci(n1bit_au_3_co), .A(A[3]), .B(B[3]), .S1(in_4), .S0(in_5), .F(out_6[3]), .Co(Co));
  xor xor_1 (V, n1bit_au_3_co, Co);
endmodule

// 4 2x1
module _4bit_2x1_MUX (
  input  [3:0] in_1,
  input  [3:0] in_2,
  input  in_3,
  output [3:0] out_4
);

  _2x1_MUX u_2x1_mux_1 (.in_1(in_3), .in_2(in_1[0]), .in_3(in_2[0]), .out_4(out_4[0]));
  _2x1_MUX u_2x1_mux_2 (.in_1(in_3), .in_2(in_1[1]), .in_3(in_2[1]), .out_4(out_4[1]));
  _2x1_MUX u_2x1_mux_3 (.in_1(in_3), .in_2(in_1[2]), .in_3(in_2[2]), .out_4(out_4[2]));
  _2x1_MUX u_2x1_mux_4 (.in_1(in_3), .in_2(in_1[3]), .in_3(in_2[3]), .out_4(out_4[3]));
endmodule

module _2x1_MUX (
  input  in_1,
  input  in_2,
  input  in_3,
  output out_4
);

  wire _0_out, _1_out, not_1_out;

  not not_1 (not_1_out, in_1);
  and _0 (_0_out, not_1_out, in_2);
  and _1 (_1_out, in_3, in_1);
  or or_1 (out_4, _0_out, _1_out);
endmodule

module _4bit_ALU (
  input  [3:0] in_1,
  input  [3:0] in_2,
  input  s2,
  input  s1,
  input  s0,
  input  Ci,
  output Co,
  output V,
  output Z,
  output S,
  output [3:0] out_11
);

  wire [3:0] n4bit_2x1_mux_1_out_4, n4bit_au_1_out_6, n4bit_lu_1_out_5, n4bit_shifter_1_out_6;

  _4bit_AU u_4bit_au_1 (.Cin(Ci), .A(in_1), .B(in_2), .in_4(s1), .in_5(s0), .out_6(n4bit_au_1_out_6), .V(V), .Co(Co));
  _4bit_LU u_4bit_lu_1 (.in_1(in_1), .in_2(in_2), .S1(s1), .S0(s0), .out_5(n4bit_lu_1_out_5));
  _4bit_shifter u_4bit_shifter_1 (
    .SLin(1'b0), .in_2(in_1), .SRin(1'b0), .S1(s1), .S0(s0), .out_6(n4bit_shifter_1_out_6));
  _4bit_2x1_MUX u_4bit_2x1_mux_1 (
    .in_1(n4bit_lu_1_out_5), .in_2(n4bit_shifter_1_out_6), .in_3(Ci), .out_4(n4bit_2x1_mux_1_out_4));
  _4bit_2x1_MUX u_4bit_2x1_mux_2 (.in_1(n4bit_au_1_out_6), .in_2(n4bit_2x1_mux_1_out_4), .in_3(s2), .out_4(out_11));
  nor nor_1 (Z, out_11[0], out_11[1], out_11[2], out_11[3]);

  assign S = out_11[3];

  // Notes on the sheet:
  //   S2== 0 산술연산 AU
  //   S2, Ci == 1,0 LU
  //   S2, ci == 1,1 shift
  //   부호비트
  //   0인지 확인
endmodule
