// Logisim project kaoshi222.circ as structural Verilog: 12 circuits, main circuit main
module main (
  input  in_1,
  output [31:0] out_2,
  output out_3,
  output [4:0] out_4,
  output [31:0] out_5,
  output out_6,
  output [4:0] out_7,
  output [31:0] out_8
);

  wire ALUSrc, bal, clk, MemtoReg, PCSrc, RegDst;
  wire [1:0] Extop;
  wire [2:0] ALUop;
  wire [4:0] multiplexer_1_out;
  wire [31:0] alu_1_out_4, balPC, extender_1_out_3, grf_1_out_8, multiplexer_4_out, multiplexer_5_out,
       ram_1_data;

  Clock clock_1 (.out(clk));
  IFU ifu_1 (
    .clk(clk), .reset(in_1), .PCSrc(PCSrc), .in_4({alu_1_out_4[31:7], out_7, alu_1_out_4[1:0]}), .bal(bal),
    .out_6(out_2), .bal_2(balPC));
  Multiplexer #(.width(5)) multiplexer_1 (
    .in0(out_2[15:11]), .in1({5{1'b1}}), .out(multiplexer_1_out), .sel(bal));  // open: en
  Multiplexer #(.width(5)) multiplexer_2 (
    .in0(out_2[20:16]), .in1(multiplexer_1_out), .out(out_4), .sel(RegDst));  // open: en
  GRF grf_1 (
    .Read_register1(out_2[25:21]), .Read_register2(out_2[20:16]), .Write_register(out_4), .in_7(out_5),
    .clk(clk), .reset(in_1), .RegWrite(out_3), .out_8(grf_1_out_8), .out_9(out_8));
  Extender extender_1 (.in_1(out_2[15:0]), .Extop(Extop), .out_3(extender_1_out_3));
  Multiplexer #(.width(32)) multiplexer_3 (.in0(multiplexer_5_out), .in1(balPC), .out(out_5), .sel(bal));  // open: en
  Controller controller_1 (
    .func(out_2[5:0]), .op(out_2[31:26]), .RegDst(RegDst), .ALUSrc(ALUSrc), .MentoReg(MemtoReg),
    .out_6(out_3), .MemWrite(out_6), .PCSrc(PCSrc), .Extop(Extop), .out_10(ALUop), .bal(bal));
  Multiplexer #(.width(32)) multiplexer_4 (
    .in0(out_8), .in1(extender_1_out_3), .out(multiplexer_4_out), .sel(ALUSrc));  // open: en
  Multiplexer #(.width(32)) multiplexer_5 (
    .in0({alu_1_out_4[31:7], out_7, alu_1_out_4[1:0]}), .in1(ram_1_data), .out(multiplexer_5_out),
    .sel(MemtoReg));  // open: en
  ALU alu_1 (
    .in_1(grf_1_out_8), .in_2(multiplexer_4_out), .ALUop(ALUop),
    .out_4({alu_1_out_4[31:7], out_7, alu_1_out_4[1:0]}));
  RAM #(.addrWidth(5), .dataWidth(32), .bus("separate")) ram_1 (
    .addr(out_7), .din(out_8), .data(ram_1_data), .str(out_6), .clk(clk));  // open: sel, ld, clr

  // Other names for the same wires on the sheet: MemAddr[4:0] = out_7; Instr[31:0] = out_2; MemData[31:0] = out_8;
  //   MemWrite = out_6; rd[4:0] = out_2[15:11]; RegAddr[4:0] = out_4; RegData[31:0] = out_5; RegWrite = out_3;
  //   reset = in_1; rs[4:0] = out_2[25:21]; rt[4:0] = out_2[20:16]

  // Notes on the sheet:
  //   func
  //   op
endmodule

module GRF (
  input  reset,
  input  RegWrite,
  input  clk,
  input  [4:0] Read_register1,
  input  [4:0] Read_register2,
  input  [4:0] Write_register,
  input  [31:0] in_7,
  output [31:0] out_8,
  output [31:0] out_9
);

  wire [31:0] r0, R1, r1_t, R2, r2_t, R3, r3_t, R4, r4_t, R5, r5_t, R6, r6_t, R7, r7_t, R8, r8_t, R9, r9_t,
       R10, r10_t, R11, r11_t, R12, r12_t, R13, r13_t, R14, r14_t, R15, r15_t, R16, r16_t, R17, r17_t, R18,
       r18_t, R19, r19_t, R20, r20_t, R21, r21_t, R22, r22_t, R23, r23_t, R24, r24_t, R25, r25_t, R26, r26_t,
       R27, r27_t, R28, r28_t, R29, r29_t, R30, r30_t, R31, r31_t;

  Demultiplexer #(.select(5), .width(32), .tristate("true")) demultiplexer_1 (
    .out1(R1), .out2(R2), .out3(R3), .out4(R4), .out5(R5), .out6(R6), .out7(R7), .out8(R8), .out9(R9),
    .out10(R10), .out11(R11), .out12(R12), .out13(R13), .out14(R14), .out15(R15), .out16(R16), .out17(R17),
    .out18(R18), .out19(R19), .out20(R20), .out21(R21), .out22(R22), .out23(R23), .out24(R24), .out25(R25),
    .out26(R26), .out27(R27), .out28(R28), .out29(R29), .out30(R30), .out31(R31), .in(in_7),
    .sel(Write_register), .en(RegWrite));  // open: out0
  Register #(.width(32)) register_1 (.D({32{1'b0}}), .Q(r0), .clk(clk), .clr(reset));  // open: en
  Register #(.width(32)) register_2 (.D(R1), .Q(r1_t), .clk(clk), .clr(reset));  // open: en
  Register #(.width(32)) register_3 (.D(R2), .Q(r2_t), .clk(clk), .clr(reset));  // open: en
  Register #(.width(32)) register_4 (.D(R3), .Q(r3_t), .clk(clk), .clr(reset));  // open: en
  Register #(.width(32)) register_5 (.D(R4), .Q(r4_t), .clk(clk), .clr(reset));  // open: en
  Register #(.width(32)) register_6 (.D(R5), .Q(r5_t), .clk(clk), .clr(reset));  // open: en
  Register #(.width(32)) register_7 (.D(R6), .Q(r6_t), .clk(clk), .clr(reset));  // open: en
  Register #(.width(32)) register_8 (.D(R7), .Q(r7_t), .clk(clk), .clr(reset));  // open: en
  Register #(.width(32)) register_9 (.D(R8), .Q(r8_t), .clk(clk), .clr(reset));  // open: en
  Register #(.width(32)) register_10 (.D(R9), .Q(r9_t), .clk(clk), .clr(reset));  // open: en
  Register #(.width(32)) register_11 (.D(R10), .Q(r10_t), .clk(clk), .clr(reset));  // open: en
  Register #(.width(32)) register_12 (.D(R11), .Q(r11_t), .clk(clk), .clr(reset));  // open: en
  Register #(.width(32)) register_13 (.D(R12), .Q(r12_t), .clk(clk), .clr(reset));  // open: en
  Register #(.width(32)) register_14 (.D(R13), .Q(r13_t), .clk(clk), .clr(reset));  // open: en
  Register #(.width(32)) register_15 (.D(R14), .Q(r14_t), .clk(clk), .clr(reset));  // open: en
  Register #(.width(32)) register_16 (.D(R15), .Q(r15_t), .clk(clk), .clr(reset));  // open: en
  Register #(.width(32)) register_17 (.D(R16), .Q(r16_t), .clk(clk), .clr(reset));  // open: en
  Register #(.width(32)) register_18 (.D(R17), .Q(r17_t), .clk(clk), .clr(reset));  // open: en
  Register #(.width(32)) register_19 (.D(R18), .Q(r18_t), .clk(clk), .clr(reset));  // open: en
  Register #(.width(32)) register_20 (.D(R19), .Q(r19_t), .clk(clk), .clr(reset));  // open: en
  Register #(.width(32)) register_21 (.D(R20), .Q(r20_t), .clk(clk), .clr(reset));  // open: en
  Register #(.width(32)) register_22 (.D(R21), .Q(r21_t), .clk(clk), .clr(reset));  // open: en
  Register #(.width(32)) register_23 (.D(R22), .Q(r22_t), .clk(clk), .clr(reset));  // open: en
  Register #(.width(32)) register_24 (.D(R23), .Q(r23_t), .clk(clk), .clr(reset));  // open: en
  Register #(.width(32)) register_25 (.D(R24), .Q(r24_t), .clk(clk), .clr(reset));  // open: en
  Register #(.width(32)) register_26 (.D(R25), .Q(r25_t), .clk(clk), .clr(reset));  // open: en
  Register #(.width(32)) register_27 (.D(R26), .Q(r26_t), .clk(clk), .clr(reset));  // open: en
  Register #(.width(32)) register_28 (.D(R27), .Q(r27_t), .clk(clk), .clr(reset));  // open: en
  Register #(.width(32)) register_29 (.D(R28), .Q(r28_t), .clk(clk), .clr(reset));  // open: en
  Register #(.width(32)) register_30 (.D(R29), .Q(r29_t), .clk(clk), .clr(reset));  // open: en
  Register #(.width(32)) register_31 (.D(R30), .Q(r30_t), .clk(clk), .clr(reset));  // open: en
  Register #(.width(32)) register_32 (.D(R31), .Q(r31_t), .clk(clk), .clr(reset));  // open: en
  Multiplexer #(.select(5), .width(32)) multiplexer_1 (
    .in0(r0), .in1(r1_t), .in2(r2_t), .in3(r3_t), .in4(r4_t), .in5(r5_t), .in6(r6_t), .in7(r7_t), .in8(r8_t),
    .in9(r9_t), .in10(r10_t), .in11(r11_t), .in12(r12_t), .in13(r13_t), .in14(r14_t), .in15(r15_t),
    .in16(r16_t), .in17(r17_t), .in18(r18_t), .in19(r19_t), .in20(r20_t), .in21(r21_t), .in22(r22_t),
    .in23(r23_t), .in24(r24_t), .in25(r25_t), .in26(r26_t), .in27(r27_t), .in28(r28_t), .in29(r29_t),
    .in30(r30_t), .in31(r31_t), .out(out_8), .sel(Read_register1));  // open: en
  Multiplexer #(.select(5), .width(32)) multiplexer_2 (
    .in0(r0), .in1(r1_t), .in2(r2_t), .in3(r3_t), .in4(r4_t), .in5(r5_t), .in6(r6_t), .in7(r7_t), .in8(r8_t),
    .in9(r9_t), .in10(r10_t), .in11(r11_t), .in12(r12_t), .in13(r13_t), .in14(r14_t), .in15(r15_t),
    .in16(r16_t), .in17(r17_t), .in18(r18_t), .in19(r19_t), .in20(r20_t), .in21(r21_t), .in22(r22_t),
    .in23(r23_t), .in24(r24_t), .in25(r25_t), .in26(r26_t), .in27(r27_t), .in28(r28_t), .in29(r29_t),
    .in30(r30_t), .in31(r31_t), .out(out_9), .sel(Read_register2));  // open: en

  // Notes on the sheet:
  //   Write data
endmodule

// Ori
module _32bit_ori (
  input  [31:0] in_1,
  input  [31:0] in_2,
  output [31:0] out_3
);

  assign out_3 = in_1 | in_2;  // OR_Gate or_1, 32 bits wide

  // Notes on the sheet:
  //   A
  //   B
endmodule

module Extender (
  input  [15:0] in_1,
  input  [1:0] Extop,
  output [31:0] out_3
);

  wire [31:0] bit_extender_1_out, bit_extender_2_out;

  assign bit_extender_1_out = {{16{1'b0}}, in_1};  // Bit_Extender bit_extender_1
  assign bit_extender_2_out = {{16{in_1[15]}}, in_1};  // Bit_Extender bit_extender_2
  Multiplexer #(.select(2), .width(32)) multiplexer_1 (
    .in0(bit_extender_1_out), .in1(bit_extender_2_out), .in2({in_1, {16{1'b0}}}), .out(out_3), .sel(Extop));  // open: in3, en

  // Notes on the sheet:
  //   imm16
endmodule

module _1bit_add (
  input  num1,
  input  num2,
  input  carry,
  output overflow,
  output sum
);

  wire and_1_out, and_2_out, and_3_out, and_4_out, and_5_out, and_6_out, and_7_out, not_1_out, not_2_out,
       not_3_out, not_4_out, not_5_out, not_6_out;

  not not_1 (not_1_out, num1);
  not not_2 (not_2_out, num2);
  not not_3 (not_3_out, num1);
  not not_4 (not_4_out, carry);
  not not_5 (not_5_out, num2);
  not not_6 (not_6_out, carry);
  and and_1 (and_1_out, num2, carry);
  and and_2 (and_2_out, num1, carry);
  or or_1 (overflow, and_1_out, and_2_out, and_3_out);
  and and_3 (and_3_out, num1, num2);
  and and_4 (and_4_out, not_1_out, not_2_out, carry);
  and and_5 (and_5_out, not_3_out, num2, not_4_out);
  and and_6 (and_6_out, num1, not_5_out, not_6_out);
  and and_7 (and_7_out, num1, num2, carry);
  or or_2 (sum, and_4_out, and_5_out, and_6_out, and_7_out);
endmodule

// Add
module _32bit_add (
  input  [31:0] in_1,
  input  [31:0] B,
  output [31:0] out_3
);

  Adder #(.width(32)) adder_1 (.a(in_1), .b(B), .out(out_3));  // open: cin, cout

  // Notes on the sheet:
  //   A
  //   sum
endmodule

// Sub
module _32bit_sub (
  input  [31:0] in_1,
  input  [31:0] in_2,
  output [31:0] out_3
);

  wire [31:0] n32bit_add_1_out_3, not_1_out;

  assign not_1_out = ~in_2;  // NOT_Gate not_1, 32 bits wide
  _32bit_add u_32bit_add_1 (.in_1(not_1_out), .B(32'h1), .out_3(n32bit_add_1_out_3));
  _32bit_add u_32bit_add_2 (.in_1(in_1), .B(n32bit_add_1_out_3), .out_3(out_3));

  // Notes on the sheet:
  //   A
  //   B
  //   difference
endmodule

module ALU (
  input  [31:0] in_1,
  input  [31:0] in_2,
  input  [2:0] ALUop,
  output [31:0] out_4
);

  wire [31:0] n32bit_add_1_out_3, n32bit_ori_1_out_3, n32bit_sub_1_out_3, wsbh_1_out_2;

  _32bit_add u_32bit_add_1 (.in_1(in_1), .B(in_2), .out_3(n32bit_add_1_out_3));
  _32bit_sub u_32bit_sub_1 (.in_1(in_1), .in_2(in_2), .out_3(n32bit_sub_1_out_3));
  _32bit_ori u_32bit_ori_1 (.in_1(in_1), .in_2(in_2), .out_3(n32bit_ori_1_out_3));
  wsbh wsbh_1 (.in_1(in_2), .out_2(wsbh_1_out_2));
  Multiplexer #(.select(3), .width(32)) multiplexer_1 (
    .in0(n32bit_add_1_out_3), .in1(n32bit_sub_1_out_3), .in2(n32bit_ori_1_out_3), .in4(wsbh_1_out_2),
    .out(out_4), .sel(ALUop));  // open: in3, in5, in6, in7, en

  // Notes on the sheet:
  //   A
  //   B
  //   Result
endmodule

module Controller (
  input  [5:0] func,
  input  [5:0] op,
  output RegDst,
  output ALUSrc,
  output MentoReg,
  output out_6,
  output MemWrite,
  output PCSrc,
  output [1:0] Extop,
  output [2:0] out_10,
  output bal
);

  wire addu_out, beq_out, lw_out, not_1_out, not_2_out, not_3_out, not_4_out, not_5_out, not_6_out,
       not_7_out, not_8_out, not_9_out, not_10_out, not_11_out, not_12_out, ori_out, subu_out, sw_out;

  not not_1 (not_1_out, func[5]);
  not not_2 (not_2_out, func[4]);
  not not_3 (not_3_out, func[3]);
  not not_4 (not_4_out, func[2]);
  not not_5 (not_5_out, func[0]);
  not not_6 (not_6_out, func[1]);
  not not_7 (not_7_out, op[5]);
  not not_8 (not_8_out, op[4]);
  not not_9 (not_9_out, op[1]);
  not not_10 (not_10_out, op[3]);
  not not_11 (not_11_out, op[2]);
  not not_12 (not_12_out, op[0]);
  and addu (addu_out, func[5], not_2_out, not_3_out, not_4_out, not_6_out, func[0], not_7_out, not_8_out, not_10_out, not_11_out, not_9_out, not_12_out);
  and subu (subu_out, func[5], not_2_out, not_3_out, not_4_out, func[1], func[0], not_7_out, not_8_out, not_10_out, not_11_out, not_9_out, not_12_out);
  and ori (ori_out, not_7_out, not_8_out, op[3], op[2], not_9_out, op[0]);
  and lw (lw_out, op[5], not_8_out, not_10_out, not_11_out, op[1], op[0]);
  and sw (sw_out, op[5], not_8_out, op[3], not_11_out, op[1], op[0]);
  and beq (beq_out, not_7_out, not_8_out, not_10_out, op[2], not_9_out, not_12_out);
  and lui (Extop[1], not_7_out, not_8_out, op[3], op[2], op[1], op[0]);
  and wsbh (out_10[2], func[5], not_2_out, not_3_out, not_4_out, not_6_out, not_5_out, not_7_out, op[4], op[3], op[2], op[1], op[0]);
  and u_bal (bal, op[0], not_9_out, not_11_out, not_10_out, not_8_out, not_7_out);
  or u_RegDst (RegDst, addu_out, out_10[2], bal, subu_out);
  or u_ALUSrc (ALUSrc, lw_out, sw_out, ori_out, Extop[1]);
  buf u_MentoReg (MentoReg, lw_out);  // OR_Gate
  buf u_MemWrite (MemWrite, sw_out);  // OR_Gate
  buf u_PCSrc (PCSrc, beq_out);  // OR_Gate
  or Extop0 (Extop[0], lw_out, beq_out, sw_out);
  // OR_Gate ADD has open pins: in0=addu_out, in1=lw_out, in2=sw_out, out=open
  or SUB (out_10[0], subu_out, beq_out);
  or ORI_2 (out_10[1], ori_out, Extop[1]);
  or RegWrite (out_6, addu_out, lw_out, subu_out, bal, ori_out, Extop[1], out_10[2]);

  // Notes on the sheet:
  //   Extop1
  //   RegWrite
  //   ALUop
endmodule

module IFU (
  input  clk,
  input  reset,
  input  PCSrc,
  input  [31:0] in_4,
  input  bal,
  output [31:0] out_6,
  output [31:0] bal_2
);

  wire and_1_out, and_2_out, comparator_1_eq, or_1_out;
  wire [31:0] bit_extender_1_out, multiplexer_1_out, multiplexer_2_out, n32bit_add_2_out_3,
       n32bit_add_3_out_3, not_1_out, register_1_q;

  assign not_1_out = ~in_4;  // NOT_Gate not_1, 32 bits wide
  and and_1 (and_1_out, not_1_out[0], not_1_out[1], not_1_out[2], not_1_out[3], not_1_out[4], not_1_out[5], not_1_out[6], not_1_out[7], not_1_out[8], not_1_out[9], not_1_out[10], not_1_out[11], not_1_out[12], not_1_out[13], not_1_out[14], not_1_out[15], not_1_out[17], not_1_out[18], not_1_out[19], not_1_out[20], not_1_out[21], not_1_out[22], not_1_out[23], not_1_out[24], not_1_out[25], not_1_out[26], not_1_out[27], not_1_out[28], not_1_out[29], not_1_out[30], not_1_out[31], not_1_out[16]);
  and and_2 (and_2_out, and_1_out, PCSrc);
  or or_1 (or_1_out, and_2_out, bal);
  Multiplexer #(.width(32)) multiplexer_1 (
    .in0(n32bit_add_2_out_3), .in1(n32bit_add_3_out_3), .out(multiplexer_1_out), .sel(or_1_out));  // open: en
  Register #(.width(32)) register_1 (.D(multiplexer_1_out), .Q(register_1_q), .clk(clk), .clr(reset));  // open: en
  _32bit_add u_32bit_add_1 (.in_1(multiplexer_2_out), .B(32'h4), .out_3(bal_2));
  assign bit_extender_1_out = {{16{out_6[15]}}, out_6[15:0]};  // Bit_Extender bit_extender_1
  Comparator #(.width(32)) comparator_1 (.a(register_1_q), .b({32{1'b0}}), .eq(comparator_1_eq));  // open: gt, lt
  _32bit_add u_32bit_add_2 (.in_1(32'h4), .B(multiplexer_2_out), .out_3(n32bit_add_2_out_3));
  Multiplexer #(.width(32)) multiplexer_2 (
    .in0(register_1_q), .in1(32'h3000), .out(multiplexer_2_out), .sel(comparator_1_eq));  // open: en
  _32bit_add u_32bit_add_3 (
    .in_1({bit_extender_1_out[29:0], 2'b00}), .B(n32bit_add_2_out_3), .out_3(n32bit_add_3_out_3));
  ROM #(.addrWidth(5), .dataWidth(32)) rom_1 (.addr(register_1_q[6:2]), .data(out_6));  // open: sel

  // Other names for the same wires on the sheet: offset[15:0] = out_6[15:0]

  // Notes on the sheet:
  //   Zero
  //   PC
  //   contents of rom_1 (hex, n*v repeats v):
  //   4110010
  //   Instr
endmodule

module wsbh (
  input  [31:0] in_1,
  output [31:0] out_2
);


  assign out_2 = {in_1[23:16], in_1[31:24], in_1[7:0], in_1[15:8]};
endmodule

module ttt (
);

  main main_1 ();  // open: in_1, out_2, out_3, out_4, out_5, out_6, out_7, out_8
endmodule
