// Logisim project p0(1).circ as structural Verilog: 3 circuits, main circuit main
module main (
  input  [6:0] in_1,
  output [6:0] out_2
);

  wire and_1_out, comparator_1_eq, comparator_1_gt, comparator_2_eq, comparator_2_gt, comparator_3_eq,
       comparator_3_lt, comparator_4_eq, comparator_4_lt, or_1_out, or_2_out, or_3_out, or_4_out;
  wire [6:0] adder_1_out, multiplexer_1_out, multiplexer_2_out, multiplexer_3_out, multiplexer_4_out,
       subtractor_1_out;

  or or_1 (or_1_out, comparator_1_gt, comparator_1_eq);
  Comparator #(.width(7), .mode("unsigned")) comparator_1 (
    .a(in_1), .b(7'b1000001), .gt(comparator_1_gt), .eq(comparator_1_eq));  // open: lt
  or or_2 (or_2_out, comparator_2_gt, comparator_2_eq);
  Comparator #(.width(7), .mode("unsigned")) comparator_2 (
    .a(in_1), .b(7'b1100001), .gt(comparator_2_gt), .eq(comparator_2_eq));  // open: lt
  Multiplexer #(.width(7)) multiplexer_1 (.in1(in_1), .out(multiplexer_1_out), .sel(or_1_out));  // open: in0, en
  Multiplexer #(.width(7)) multiplexer_2 (.in1(in_1), .out(multiplexer_2_out), .sel(or_2_out));  // open: in0, en
  Comparator #(.width(7), .mode("unsigned")) comparator_3 (
    .a(multiplexer_1_out), .b(7'b1011010), .eq(comparator_3_eq), .lt(comparator_3_lt));  // open: gt
  Comparator #(.width(7), .mode("unsigned")) comparator_4 (
    .a(multiplexer_2_out), .b(7'b1111010), .eq(comparator_4_eq), .lt(comparator_4_lt));  // open: gt
  or or_3 (or_3_out, comparator_3_eq, comparator_3_lt);
  or or_4 (or_4_out, comparator_4_eq, comparator_4_lt);
  Multiplexer #(.width(7)) multiplexer_3 (.in1(in_1), .out(multiplexer_3_out), .sel(or_3_out));  // open: in0, en
  Multiplexer #(.width(7)) multiplexer_4 (.in1(in_1), .out(multiplexer_4_out), .sel(or_4_out));  // open: in0, en
  Adder #(.width(7)) adder_1 (.a(multiplexer_3_out), .b(7'b0100000), .out(adder_1_out));  // open: cin, cout
  and and_1 (and_1_out, or_3_out, or_1_out);
  Subtractor #(.width(7)) subtractor_1 (
    .a(multiplexer_4_out), .b(7'b0100000), .out(subtractor_1_out));  // open: bin, bout
  Multiplexer #(.width(7)) multiplexer_5 (
    .in0(subtractor_1_out), .in1(adder_1_out), .out(out_2), .sel(and_1_out));  // open: en
endmodule

module letter (
  input  [6:0] in_1,
  output [6:0] out_2
);

  wire and_1_out, and_2_out, comparator_1_eq, comparator_1_gt, comparator_2_eq, comparator_2_gt,
       comparator_3_eq, comparator_3_lt, comparator_4_eq, comparator_4_lt, not_1_out, not_2_out, or_1_out,
       or_2_out, or_3_out, or_4_out;
  wire [6:0] adder_1_out, multiplexer_1_out, multiplexer_2_out, multiplexer_3_out, multiplexer_4_out,
       multiplexer_5_out, subtractor_1_out;

  Comparator #(.width(7), .mode("unsigned")) comparator_1 (
    .a(in_1), .b(7'b1000001), .gt(comparator_1_gt), .eq(comparator_1_eq));  // open: lt
  or or_1 (or_1_out, comparator_1_gt, comparator_1_eq);
  Comparator #(.width(7), .mode("unsigned")) comparator_2 (
    .a(in_1), .b(7'b1100001), .gt(comparator_2_gt), .eq(comparator_2_eq));  // open: lt
  or or_2 (or_2_out, comparator_2_gt, comparator_2_eq);
  Multiplexer #(.width(7)) multiplexer_1 (.in1(in_1), .out(multiplexer_1_out), .sel(or_1_out));  // open: in0, en
  Multiplexer #(.width(7)) multiplexer_2 (.in1(in_1), .out(multiplexer_2_out), .sel(or_2_out));  // open: in0, en
  not not_1 (not_1_out, or_1_out);
  not not_2 (not_2_out, or_2_out);
  Comparator #(.width(7), .mode("unsigned")) comparator_3 (
    .a(multiplexer_1_out), .b(7'b1011010), .eq(comparator_3_eq), .lt(comparator_3_lt));  // open: gt
  Comparator #(.width(7), .mode("unsigned")) comparator_4 (
    .a(multiplexer_2_out), .b(7'b1111010), .eq(comparator_4_eq), .lt(comparator_4_lt));  // open: gt
  and and_1 (and_1_out, not_1_out, not_2_out);
  or or_3 (or_3_out, comparator_3_eq, comparator_3_lt);
  or or_4 (or_4_out, comparator_4_eq, comparator_4_lt);
  Multiplexer #(.width(7)) multiplexer_3 (.in1(in_1), .out(multiplexer_3_out), .sel(or_3_out));  // open: in0, en
  Multiplexer #(.width(7)) multiplexer_4 (.in1(in_1), .out(multiplexer_4_out), .sel(or_4_out));  // open: in0, en
  Adder #(.width(7)) adder_1 (.a(multiplexer_3_out), .b(7'b0100000), .out(adder_1_out));  // open: cin, cout
  and and_2 (and_2_out, or_3_out, or_1_out);
  Subtractor #(.width(7)) subtractor_1 (
    .a(multiplexer_4_out), .b(7'b0100000), .out(subtractor_1_out));  // open: bin, bout
  Multiplexer #(.width(7)) multiplexer_5 (
    .in0(subtractor_1_out), .in1(adder_1_out), .out(multiplexer_5_out), .sel(and_2_out));  // open: en
  Multiplexer #(.width(7)) multiplexer_6 (
    .in0(multiplexer_5_out), .in1(in_1), .out(out_2), .sel(and_1_out));  // open: en
endmodule

module t1 (
  input  [6:0] in_1,
  output [6:0] out_2
);

  wire and_1_out, comparator_1_eq, comparator_1_gt, comparator_2_eq, comparator_2_gt, comparator_3_eq,
       comparator_3_lt, comparator_4_eq, comparator_4_lt, or_1_out, or_2_out, or_3_out, or_4_out;
  wire [6:0] adder_1_out, multiplexer_1_out, multiplexer_2_out, multiplexer_3_out, multiplexer_4_out,
       subtractor_1_out;

  or or_1 (or_1_out, comparator_1_gt, comparator_1_eq);
  Comparator #(.width(7), .mode("unsigned")) comparator_1 (
    .a(in_1), .b(7'b1000001), .gt(comparator_1_gt), .eq(comparator_1_eq));  // open: lt
  Comparator #(.width(7), .mode("unsigned")) comparator_2 (
    .a(in_1), .b(7'b1100001), .gt(comparator_2_gt), .eq(comparator_2_eq));  // open: lt
  or or_2 (or_2_out, comparator_2_gt, comparator_2_eq);
  Multiplexer #(.width(7), .disabled(0)) multiplexer_1 (
    .in1(in_1), .out(multiplexer_1_out), .sel(or_1_out));  // open: in0, en
  Multiplexer #(.width(7), .disabled(0)) multiplexer_2 (
    .in1(in_1), .out(multiplexer_2_out), .sel(or_2_out));  // open: in0, en
  Comparator #(.width(7), .mode("unsigned")) comparator_3 (
    .a(multiplexer_1_out), .b(7'b1011010), .eq(comparator_3_eq), .lt(comparator_3_lt));  // open: gt
  Comparator #(.width(7), .mode("unsigned")) comparator_4 (
    .a(multiplexer_2_out), .b(7'b1111010), .eq(comparator_4_eq), .lt(comparator_4_lt));  // open: gt
  or or_3 (or_3_out, comparator_3_eq, comparator_3_lt);
  or or_4 (or_4_out, comparator_4_eq, comparator_4_lt);
  Multiplexer #(.width(7), .disabled(0)) multiplexer_3 (
    .in1(in_1), .out(multiplexer_3_out), .sel(or_3_out));  // open: in0, en
  Multiplexer #(.width(7), .disabled(0)) multiplexer_4 (
    .in1(in_1), .out(multiplexer_4_out), .sel(or_4_out));  // open: in0, en
  Adder #(.width(7)) adder_1 (.a(multiplexer_3_out), .b(7'b0100000), .out(adder_1_out));  // open: cin, cout
  and and_1 (and_1_out, or_3_out, or_1_out);
  Subtractor #(.width(7)) subtractor_1 (
    .a(multiplexer_4_out), .b(7'b0100000), .out(subtractor_1_out));  // open: bin, bout
  Multiplexer #(.width(7), .disabled(0)) multiplexer_5 (
    .in0(subtractor_1_out), .in1(adder_1_out), .out(out_2), .sel(and_1_out));  // open: en
endmodule
