// Logisim project p0(2).circ as structural Verilog: 2 circuits, main circuit main
module main (
  input  [1:0] in_1,
  input  clk,
  input  reset,
  output [1:0] out_4
);

  wire and_1_out, and_2_out, and_3_out, and_4_out, and_5_out, and_6_out, and_7_out, and_8_out, and_9_out,
       and_10_out, and_11_out, and_12_out, and_13_out, and_14_out, not_1_out, not_2_out, not_3_out,
       not_4_out, not_5_out, not_6_out, not_7_out, not_8_out, not_9_out, not_10_out, not_11_out, not_12_out,
       not_13_out, not_14_out, not_15_out, not_16_out, not_17_out, not_18_out, not_19_out, not_20_out,
       not_21_out, not_22_out, not_23_out, not_24_out, not_25_out, not_26_out, not_27_out, not_28_out,
       not_29_out, not_30_out, not_31_out, not_32_out, not_33_out, not_34_out, not_35_out, not_36_out,
       not_37_out, not_38_out, not_39_out, not_40_out, not_41_out, or_1_out, or_2_out, or_3_out, s0_q, s1_q,
       s2_q;

  not not_1 (not_1_out, s2_q);
  not not_2 (not_2_out, s1_q);
  not not_3 (not_3_out, s0_q);
  not not_4 (not_4_out, in_1[0]);
  not not_5 (not_5_out, s1_q);
  not not_6 (not_6_out, s0_q);
  not not_7 (not_7_out, in_1[1]);
  not not_8 (not_8_out, in_1[0]);
  not not_9 (not_9_out, s1_q);
  not not_10 (not_10_out, s0_q);
  not not_11 (not_11_out, in_1[0]);
  not not_12 (not_12_out, s1_q);
  not not_13 (not_13_out, in_1[0]);
  not not_14 (not_14_out, s2_q);
  not not_15 (not_15_out, in_1[0]);
  not not_16 (not_16_out, s1_q);
  not not_17 (not_17_out, in_1[1]);
  not not_18 (not_18_out, s2_q);
  not not_19 (not_19_out, s0_q);
  not not_20 (not_20_out, in_1[1]);
  not not_21 (not_21_out, s1_q);
  not not_22 (not_22_out, s1_q);
  not not_23 (not_23_out, s0_q);
  not not_24 (not_24_out, in_1[1]);
  not not_25 (not_25_out, in_1[0]);
  not not_26 (not_26_out, s2_q);
  not not_27 (not_27_out, s0_q);
  not not_28 (not_28_out, in_1[1]);
  not not_29 (not_29_out, s0_q);
  not not_30 (not_30_out, in_1[1]);
  not not_31 (not_31_out, in_1[0]);
  not not_32 (not_32_out, s1_q);
  not not_33 (not_33_out, in_1[1]);
  not not_34 (not_34_out, in_1[0]);
  not not_35 (not_35_out, s2_q);
  not not_36 (not_36_out, in_1[1]);
  not not_37 (not_37_out, in_1[0]);
  and and_1 (and_1_out, not_1_out, not_2_out, not_3_out, in_1[1], not_4_out);
  and and_2 (and_2_out, s2_q, not_5_out, not_6_out, not_7_out, not_8_out);
  and and_3 (and_3_out, s2_q, not_9_out, s0_q, in_1[1], in_1[0]);
  and and_4 (and_4_out, s2_q, not_10_out, in_1[1], not_11_out);
  and and_5 (and_5_out, not_12_out, s0_q, in_1[1], not_13_out);
  and and_6 (and_6_out, not_14_out, s1_q, in_1[1], not_15_out);
  and and_7 (and_7_out, not_16_out, s0_q, not_17_out, in_1[0]);
  and and_8 (and_8_out, not_18_out, s1_q, not_19_out, not_20_out, in_1[0]);
  and and_9 (and_9_out, s2_q, not_21_out, s0_q, in_1[1], in_1[0]);
  and and_10 (and_10_out, not_22_out, not_23_out, not_24_out, not_25_out);
  and and_11 (and_11_out, not_26_out, s1_q, not_27_out, not_28_out, in_1[0]);
  and and_12 (and_12_out, s2_q, not_29_out, not_30_out, not_31_out);
  and and_13 (and_13_out, not_32_out, s0_q, not_33_out, not_34_out);
  and and_14 (and_14_out, not_35_out, s1_q, not_36_out, not_37_out);
  or or_1 (or_1_out, and_7_out, and_8_out, and_9_out);
  or or_2 (or_2_out, and_10_out, and_11_out, and_12_out, and_13_out, and_14_out);
  or or_3 (or_3_out, and_1_out, and_2_out, and_3_out, and_4_out, and_5_out, and_6_out);
  D_Flip_Flop s2 (.clk(clk), .D(or_3_out), .Q(s2_q), .reset(reset));  // open: Qn, preset, en
  D_Flip_Flop s1 (.clk(clk), .D(or_1_out), .Q(s1_q), .reset(reset));  // open: Qn, preset, en
  D_Flip_Flop s0 (.clk(clk), .D(or_2_out), .Q(s0_q), .reset(reset));  // open: Qn, preset, en
  not not_38 (not_38_out, s2_q);
  not not_39 (not_39_out, s0_q);
  and o0 (out_4[0], not_38_out, s1_q, not_39_out, not_40_out, in_1[0]);
  not not_40 (not_40_out, in_1[1]);
  not not_41 (not_41_out, s1_q);
  and o1 (out_4[1], s2_q, not_41_out, s0_q, in_1[1], in_1[0]);
endmodule

module mips (
  input  [1:0] in_1,
  input  clk,
  input  reset,
  output [1:0] out_4
);

  wire and_1_out, and_2_out, and_3_out, and_4_out, and_5_out, and_6_out, and_7_out, and_8_out, and_9_out,
       and_10_out, and_11_out, and_12_out, and_13_out, and_14_out, not_1_out, not_2_out, not_3_out,
       not_4_out, not_5_out, not_6_out, not_7_out, not_8_out, not_9_out, not_10_out, not_11_out, not_12_out,
       not_13_out, not_14_out, not_15_out, not_16_out, not_17_out, not_18_out, not_19_out, not_20_out,
       not_21_out, not_22_out, not_23_out, not_24_out, not_25_out, not_26_out, not_27_out, not_28_out,
       not_29_out, not_30_out, not_31_out, not_32_out, not_33_out, not_34_out, not_35_out, not_36_out,
       not_37_out, not_38_out, not_39_out, not_40_out, not_41_out, or_1_out, or_2_out, or_3_out, s0_q, s1_q,
       s2_q;

  not not_1 (not_1_out, s2_q);
  not not_2 (not_2_out, s1_q);
  not not_3 (not_3_out, s0_q);
  not not_4 (not_4_out, in_1[0]);
  not not_5 (not_5_out, s1_q);
  not not_6 (not_6_out, s0_q);
  not not_7 (not_7_out, in_1[1]);
  not not_8 (not_8_out, in_1[0]);
  not not_9 (not_9_out, s1_q);
  not not_10 (not_10_out, s0_q);
  not not_11 (not_11_out, in_1[0]);
  not not_12 (not_12_out, s1_q);
  not not_13 (not_13_out, in_1[0]);
  not not_14 (not_14_out, s2_q);
  not not_15 (not_15_out, in_1[0]);
  not not_16 (not_16_out, s1_q);
  not not_17 (not_17_out, in_1[1]);
  not not_18 (not_18_out, s2_q);
  not not_19 (not_19_out, s0_q);
  not not_20 (not_20_out, in_1[1]);
  not not_21 (not_21_out, s1_q);
  not not_22 (not_22_out, s1_q);
  not not_23 (not_23_out, s0_q);
  not not_24 (not_24_out, in_1[1]);
  not not_25 (not_25_out, in_1[0]);
  not not_26 (not_26_out, s2_q);
  not not_27 (not_27_out, s0_q);
  not not_28 (not_28_out, in_1[1]);
  not not_29 (not_29_out, s0_q);
  not not_30 (not_30_out, in_1[1]);
  not not_31 (not_31_out, in_1[0]);
  not not_32 (not_32_out, s1_q);
  not not_33 (not_33_out, in_1[1]);
  not not_34 (not_34_out, in_1[0]);
  not not_35 (not_35_out, s2_q);
  not not_36 (not_36_out, in_1[1]);
  not not_37 (not_37_out, in_1[0]);
  and and_1 (and_1_out, not_1_out, not_2_out, not_3_out, in_1[1], not_4_out);
  and and_2 (and_2_out, s2_q, not_5_out, not_6_out, not_7_out, not_8_out);
  and and_3 (and_3_out, s2_q, not_9_out, s0_q, in_1[1], in_1[0]);
  and and_4 (and_4_out, s2_q, not_10_out, in_1[1], not_11_out);
  and and_5 (and_5_out, not_12_out, s0_q, in_1[1], not_13_out);
  and and_6 (and_6_out, not_14_out, s1_q, in_1[1], not_15_out);
  and and_7 (and_7_out, not_16_out, s0_q, not_17_out, in_1[0]);
  and and_8 (and_8_out, not_18_out, s1_q, not_19_out, not_20_out, in_1[0]);
  and and_9 (and_9_out, s2_q, not_21_out, s0_q, in_1[1], in_1[0]);
  and and_10 (and_10_out, not_22_out, not_23_out, not_24_out, not_25_out);
  and and_11 (and_11_out, not_26_out, s1_q, not_27_out, not_28_out, in_1[0]);
  and and_12 (and_12_out, s2_q, not_29_out, not_30_out, not_31_out);
  and and_13 (and_13_out, not_32_out, s0_q, not_33_out, not_34_out);
  and and_14 (and_14_out, not_35_out, s1_q, not_36_out, not_37_out);
  or or_1 (or_1_out, and_7_out, and_8_out, and_9_out);
  or or_2 (or_2_out, and_10_out, and_11_out, and_12_out, and_13_out, and_14_out);
  or or_3 (or_3_out, and_1_out, and_2_out, and_3_out, and_4_out, and_5_out, and_6_out);
  D_Flip_Flop s2 (.clk(clk), .D(or_3_out), .Q(s2_q), .reset(reset));  // open: Qn, preset, en
  D_Flip_Flop s1 (.clk(clk), .D(or_1_out), .Q(s1_q), .reset(reset));  // open: Qn, preset, en
  D_Flip_Flop s0 (.clk(clk), .D(or_2_out), .Q(s0_q), .reset(reset));  // open: Qn, preset, en
  not not_38 (not_38_out, s2_q);
  and o0 (out_4[0], not_38_out, s1_q, not_39_out, not_40_out, in_1[0]);
  not not_39 (not_39_out, s0_q);
  not not_40 (not_40_out, in_1[1]);
  not not_41 (not_41_out, s1_q);
  and o1 (out_4[1], s2_q, not_41_out, s0_q, in_1[1], in_1[0]);
endmodule
