// Logisim project p0(3).circ as structural Verilog: 4 circuits, main circuit main
module main (
  input  [31:0] in_1,
  output [31:0] out_2
);

  FF_a_b_c_d_Mj_s ff_a_b_c_d_mj_s_1 (
    .a(8'hef), .b(8'h98), .c(8'h10), .d(8'h67), .mj(in_1[31:24]), .s(3'b001), .out_7(out_2[7:0]));
  FF_a_b_c_d_Mj_s ff_a_b_c_d_mj_s_2 (
    .a(8'h98), .b(8'h10), .c(8'h67), .d(8'hef), .mj(in_1[23:16]), .s(3'b000), .out_7(out_2[15:8]));
  FF_a_b_c_d_Mj_s ff_a_b_c_d_mj_s_3 (
    .a(8'h67), .b(8'hef), .c(8'h98), .d(8'h10), .mj(in_1[7:0]), .s(3'b000), .out_7(out_2[31:24]));
  FF_a_b_c_d_Mj_s ff_a_b_c_d_mj_s_4 (
    .a(8'h10), .b(8'h67), .c(8'hef), .d(8'h98), .mj(in_1[15:8]), .s(3'b001), .out_7(out_2[23:16]));

  // Notes on the sheet:
  //   a
  //   b
  //   c
  //   d
endmodule

module F_X_Y_Z (
  input  [7:0] X,
  input  [7:0] Y,
  input  [7:0] Z,
  output [7:0] out_4
);

  wire [7:0] and_1_out, and_2_out, not_1_out;

  assign and_1_out = X & Y;  // AND_Gate and_1, 8 bits wide
  assign not_1_out = ~X;  // NOT_Gate not_1, 8 bits wide
  assign and_2_out = not_1_out & Z;  // AND_Gate and_2, 8 bits wide
  assign out_4 = and_1_out | and_2_out;  // OR_Gate or_1, 8 bits wide
endmodule

// FF(a,b,c,d,Mj,s
module FF_a_b_c_d_Mj_s (
  input  [7:0] a,
  input  [7:0] b,
  input  [7:0] c,
  input  [7:0] d,
  input  [7:0] mj,
  input  [2:0] s,
  output [7:0] out_7
);

  wire [7:0] adder_1_out, adder_2_out, f_x_y_z_1_out_4, shifter_1_out;

  F_X_Y_Z f_x_y_z_1 (.X(b), .Y(c), .Z(d), .out_4(f_x_y_z_1_out_4));
  Adder adder_1 (.a(a), .b(f_x_y_z_1_out_4), .out(adder_1_out));  // open: cin, cout
  Adder adder_2 (.a(adder_1_out), .b(mj), .out(adder_2_out));  // open: cin, cout
  Shifter shifter_1 (.in(adder_2_out), .\dist (s), .out(shifter_1_out));
  Adder adder_3 (.a(b), .b(shifter_1_out), .out(out_7));  // open: cin, cout
endmodule

module code (
  input  [31:0] in_1,
  output [31:0] out_2
);

  FF_a_b_c_d_Mj_s ff_a_b_c_d_mj_s_1 (
    .a(out_2[23:16]), .b(out_2[15:8]), .c(8'h10), .d(out_2[31:24]), .mj(in_1[7:0]), .s(3'b001),
    .out_7(out_2[7:0]));
  FF_a_b_c_d_Mj_s ff_a_b_c_d_mj_s_2 (
    .a(8'h98), .b(8'h10), .c(out_2[31:24]), .d(out_2[23:16]), .mj(in_1[15:8]), .s(3'b000), .out_7(out_2[15:8]));
  FF_a_b_c_d_Mj_s ff_a_b_c_d_mj_s_3 (
    .a(8'h67), .b(8'hef), .c(8'h98), .d(8'h10), .mj(in_1[31:24]), .s(3'b000), .out_7(out_2[31:24]));
  FF_a_b_c_d_Mj_s ff_a_b_c_d_mj_s_4 (
    .a(8'h10), .b(out_2[31:24]), .c(8'hef), .d(8'h98), .mj(in_1[23:16]), .s(3'b001), .out_7(out_2[23:16]));

  // Notes on the sheet:
  //   a
  //   b
  //   d
  //   c
  //   d
  //   c
  //   a
  //   b
endmodule
